# Fritzing sketch Sample Circuit Diagram (saved by Fritzing 0.9.5d)
breadboards: 1

parts:
  S3 = Pushbutton [package="[THT]"]
  S2 = Pushbutton [package="[THT]"]
  S1 = Pushbutton [package="[THT]"]
  S8 = Pushbutton [package="[THT]"]
  S7 = Pushbutton [package="[THT]"]
  S6 = Pushbutton [package="[THT]"]
  S5 = Pushbutton [package="[THT]"]
  T1 = Arduino Uno (Rev3) [part_number="UNO Rev3"]
  R2 = Resistor [tolerance=±5% resistance=10k package=THT]
  R3 = Resistor [tolerance=±5% resistance=10k package=THT]
  R5 = Resistor [tolerance=±5% resistance=10k package=THT]
  R4 = Resistor [tolerance=±5% resistance=10k package=THT]
  R6 = Resistor [tolerance=±5% resistance=10k package=THT]
  R8 = Resistor [tolerance=±5% resistance=10k package=THT]
  R1 = Resistor [tolerance=±5% resistance=10k package=THT]
  U1 = LCD-16X2 [part_number="LCD 16X2" package=lcd-16x2]
  R9 = Resistor [tolerance=±5% resistance=220 package=THT]
  R10 = Trimmer Potentiometer [maximum_resistance=10kΩ package=THT]
  U2 = ESP8266 WiFi Module [part_number=ESP8266]
  S9 = Pushbutton [package=THT]
  R7 = Resistor [tolerance=±5% resistance=10k package=THT]
  S4 = Pushbutton [package="[THT]"]
  RE1 = KY-040 Rotary encoder [package=THT]

nets:
  N1: S3.Pin_1, S3.Pin_2, T1.A3, R3.Pin_0
  3V3: S3.Pin_3, S3.Pin_4, S2.Pin_3, S2.Pin_4, S1.Pin_3, S1.Pin_4, S8.Pin_3, S8.Pin_4, S7.Pin_3, S7.Pin_4, S6.Pin_3, S6.Pin_4, S5.Pin_3, S5.Pin_4, T1.3V3, U2.VCC, U2.CH_PD, S4.Pin_3, S4.Pin_4
  N2: S2.Pin_1, S2.Pin_2, T1.A4/SDA, R2.Pin_0
  N3: S1.Pin_1, S1.Pin_2, T1.A5/SCL, R1.Pin_0
  N4: S8.Pin_1, S8.Pin_2, T1.D6_PWM, R8.Pin_0
  N5: S7.Pin_1, S7.Pin_2, T1.D7, R7.Pin_0
  N6: S6.Pin_1, S6.Pin_2, T1.A0, R6.Pin_0
  N7: S5.Pin_1, S5.Pin_2, T1.A1, R5.Pin_0
  N8: T1.A2, R4.Pin_0, S4.Pin_1, S4.Pin_2
  N9: T1.D8, U1.DB7
  N10: T1.D9_PWM, U1.DB6
  N11: T1.D10_PWM/SS, U1.DB5
  N12: T1.D11_PWM/MOSI, U1.DB4
  N13: T1.D12/MISO, U1.E
  N14: T1.D13/SCK, U1.RS
  N15: T1.D0/RX, U2.TXD
  N16: T1.D1/TX, U2.RXD
  N17: T1.D2, RE1.CLK
  N18: T1.D3_PWM, RE1.DT
  N19: T1.D4, RE1.SW
  5V: T1.5V, U1.VDD, R9.Pin_0, R10.leg1, RE1.Vcc
  GND: T1.GND, R2.Pin_1, R3.Pin_1, R5.Pin_1, R4.Pin_1, R6.Pin_1, R8.Pin_1, R1.Pin_1, U1.VSS, U1.R_W, U1.K, R10.leg2, U2.GND, S9.leg1, R7.Pin_1, RE1.GND
  N20: U1.VO, R10.wiper
  N21: U1.A, R9.Pin_1
  N22: U2.REST, S9.leg0

custom parts:
  KY-040 Rotary encoder: KY-040 Rotary Encoder with switch on breakout borad from AZ Delivery
